# Fritzing sketch lazy-tv (saved by Fritzing 0.9.4)
breadboards: 1

parts:
  Part1 = Arduino Nano (Rev3.0)
  Power_plug1 = Power plug
  M1 = RioRand LM2596
  J1 = Basic Servo
  IR1 = TSOP312.., 314.. [package=THT]

nets:
  GND: Part1.GND, M1.Pin_4, J1.gnd, IR1.GND
  N1: Part1.D9, J1.pulse
  VIN: Part1.VIN, M1.Pin_3, J1.vcc
  N2: Part1.5V, IR1.Vs
  N3: Part1.A7, IR1.Data
  N4: Power_plug1.GND, M1.Pin_2
  N5: Power_plug1.VCC, M1.Pin_1
